// Logisim project 8bitBoothMultiplier.circ as structural Verilog: 1 circuit, main circuit BoothMult
module BoothMult (
  input  [7:0] FirstOperand,
  input  [7:0] SecondOperand,
  output [15:0] Result
);


  // Other names for the same wires on the sheet: A[7:0] = FirstOperand; B[7:0] = SecondOperand; C[15:0] = Result
endmodule
