// Logisim project CustomAdder.circ as structural Verilog: 1 circuit, main circuit CustomAdder
module CustomAdder (
  input  [15:0] FirstOperand,
  input  [15:0] SecondOperand,
  input  CarryIn,
  output [15:0] Result,
  output CarryOut
);


  // Other names for the same wires on the sheet: A[15:0] = FirstOperand; B[15:0] = SecondOperand; C[15:0] = Result;
  //   CIN = CarryIn; COUT = CarryOut
endmodule
