// Logisim project CustomMultiplier.circ as structural Verilog: 1 circuit, main circuit CustomMultiplier
module CustomMultiplier (
  input  [7:0] FirstOperand,
  input  [7:0] SecondOperand,
  input  Clock,
  output [15:0] Result,
  output Done
);


  // Other names for the same wires on the sheet: A[7:0] = FirstOperand; B[7:0] = SecondOperand; C[15:0] = Result;
  //   clk = Clock
endmodule
