// Logisim project MatrixCalculation.circ as structural Verilog: 1 circuit, main circuit main
module main (
  input  [31:0] A,
  input  [31:0] X,
  input  [31:0] C,
  output [63:0] Result
);

  // BoothMult boothmult_1: pin names not known
  // Mult mult_1: pin names not known
  // Add add_1: pin names not known

  // Other names for the same wires on the sheet: A_1_1[7:0] = A[7:0]; A_1_2[7:0] = A[15:8]; A_2_1[7:0] = A[23:16];
  //   A_2_2[7:0] = A[31:24]; B_1_1[7:0] = C[7:0]; B_1_2[7:0] = C[15:8]; B_2_1[7:0] = C[23:16]; B_2_2[7:0] = C[31:24];
  //   Result_1_1[15:0] = Result[15:0]; Result_1_2[15:0] = Result[31:16]; Result_2_1[15:0] = Result[47:32];
  //   Result_2_2[15:0] = Result[63:48]; X_1_1[7:0] = X[7:0]; X_1_2[7:0] = X[15:8]; X_2_1[7:0] = X[23:16];
  //   X_2_2[7:0] = X[31:24]

  // Notes on the sheet:
  //   Please don't change places of inputs and outputs
endmodule
