// Logisim project Tester.circ as structural Verilog: 1 circuit, main circuit Tester
module Tester (
);

  wire clock_1_out;
  wire [7:0] adder_1_out, Address;
  wire [31:0] A, C, X;
  wire [63:0] Result;

  Register register_1 (.D(adder_1_out), .Q(Address), .clr(clock_1_out));  // open: en, clk
  Adder adder_1 (.a(Address), .b(8'h4), .out(adder_1_out));  // open: cin, cout
  Clock clock_1 (.out(clock_1_out));
  ROM #(.dataWidth(32)) rom_1 (.addr(Address), .data(A));
  MatrixCalculation_main main_1 (.A(A), .X(X), .C(C), .Result(Result));
endmodule
